# Fritzing sketch Sketch_Pisca_Pisca (saved by Fritzing 0.7.10b)
breadboards: 1

parts:
  Arduino1 = Arduino
  LED1 = red smd LED [package="1206 [SMD]"]
  LED2 = yellow smd LED [package="0603 [SMD]"]
  LED3 = green smd LED [package="1206 [SMD]"]
  LED4 = red smd LED [package="1206 [SMD]"]
  LED5 = yellow smd LED [package="0603 [SMD]"]
  LED6 = green smd LED [package="1206 [SMD]"]
  LED7 = yellow smd LED [package="0603 [SMD]"]

nets:
  N1: Arduino1.GND, LED1.anode, LED2.anode, LED3.anode, LED4.anode, LED5.anode, LED6.anode, LED7.anode
  N2: Arduino1.D13, LED7.cathode
  N3: Arduino1.D12, LED4.cathode
  N4: Arduino1.D11, LED5.cathode
  N5: Arduino1.D10, LED6.cathode
  N6: Arduino1.D9, LED1.cathode
  N7: Arduino1.D8, LED2.cathode
  N8: Arduino1.D7, LED3.cathode
