# Fritzing sketch automatizado (saved by Fritzing 0.7.1b)
breadboards: 1

parts:
  Arduino1 = Arduino
  R1 = Resistor [tolerance=±5% resistance=220 package=THT]
  R2 = Photocell (LDR) [package=THT]
  LED1 = LED - 5mm [color="Red (633nm)" package="5 mm [THT]"]
  J1 = Piezo Speaker

nets:
  N1: Arduino1.GND, R1.Pin_0, LED1.anode, J1.pin2
  N2: Arduino1.D13, LED1.cathode
  N3: Arduino1.D7, J1.pin1
  N4: Arduino1.+5V, R2.pin_1
  N5: Arduino1.A0, R1.Pin_1, R2.pin_0
